# Fritzing sketch shema-electronique (saved by Fritzing 0.9.3b)

parts:
  raspberry_pi_4 = Raspberry Pi 4 [part_number=RPI-4-b]
  J1 = Basic Servo
  M2 = ESC
  920KV_Motor2 = DJI 920 KV Motor
  Power_plug3 = Power plug  # not connected
  S1 = Pushbutton [package="[THT]"]
  R1 = Resistor [tolerance=±5% resistance=23 package="0603 [SMD]"]

nets (from the breadboard view):
  3V3: raspberry_pi_4.3v3, raspberry_pi_4.3V3, S1.Pin_2
  N1: raspberry_pi_4.GPIO13, M2.DATA
  N2: raspberry_pi_4.GPIO21, R1.Pin_0
  GND: raspberry_pi_4.GND, J1.gnd, M2.GND
  N3: raspberry_pi_4.GPIO12, J1.pulse
  VCC: J1.vcc, M2.5V
  N4: M2.U, 920KV_Motor2.u
  N5: M2.V, 920KV_Motor2.v
  N6: M2.W, 920KV_Motor2.w
  N7: S1.Pin_3, S1.Pin_4, R1.Pin_1

notes:
  INPUT 7,2V
  ECS 25A
  BRUSHLESS MOTOR
  SERVO FOR CAR DIRECTION
  RASPBERRY 4
  SHUTDOWN BUTTON

custom parts:
  Raspberry Pi 4: The RPi4, a faster version of the awesome Raspberry Pi 2 B ARM Board with 40 pin gpio. Ready for special Raspberry Pi B+ and RPi2 Hat (Hardware attached (on) top)
  DJI 920 KV Motor: DJI Brushless Outrunner 2212/920K Motor F330-550

// code stored in the sketch: Untitled.ino
import RPi.GPIO as GPIO
import time



GPIO.setmode(GPIO.BCM)


TRIG = 23
ECHO = 24
LED1 = 13
LED2 = 19
buzzer = 26
motor1a= 3
motor1b= 4
motor2a= 20
motor2b= 21
motor= 25
i=0


GPIO.setup(TRIG,GPIO.OUT)
GPIO.setup(ECHO,GPIO.IN)


GPIO.setup(LED1,GPIO.OUT)
GPIO.setup(LED2,GPIO.OUT)
GPIO.setup(buzzer,GPIO.OUT)
GPIO.setup(motor1a,GPIO.OUT)
GPIO.setup(motor1b,GPIO.OUT)
GPIO.setup(motor2a,GPIO.OUT)
GPIO.setup(motor2b,GPIO.OUT)
GPIO.setup(motor,GPIO.OUT)






GPIO.output(TRIG, False)
print("Calibrating.....")
print("Place the object......")




while True:
    GPIO.output(TRIG, True)
    time.sleep(0.00001)
    GPIO.output(TRIG, False)


    while GPIO.input(ECHO)==0:
        pulse_start = time.time()


    while GPIO.input(ECHO)==1:
        pulse_end = time.time()


    pulse_duration = pulse_end - pulse_start


    distance = pulse_duration * 17150


    distance = round(distance+1.15, 2)
  
    if distance<=10:
        print("distance:",distance,"cm")
        GPIO.output(LED1,GPIO.HIGH)
        GPIO.output(LED2,GPIO.LOW)
        GPIO.output(buzzer,GPIO.HIGH)
        GPIO.output(motor1a,GPIO.HIGH)
        GPIO.output(motor1b,GPIO.LOW)
        GPIO.output(motor2a,GPIO.HIGH)
        GPIO.output(motor2b,GPIO.LOW)
        GPIO.output(motor,GPIO.HIGH)
        time.sleep(1)
        GPIO.output(buzzer,GPIO.LOW)
        
    else:
        print("place the object....")
        GPIO.output(LED1,GPIO.LOW)
        GPIO.output(LED2,GPIO.HIGH)
        GPIO.output(buzzer,GPIO.LOW)
        GPIO.output(motor1a,GPIO.LOW)
        GPIO.output(motor1b,GPIO.HIGH)
        GPIO.output(motor2a,GPIO.LOW)
        GPIO.output(motor2b,GPIO.HIGH)
        GPIO.output(motor,GPIO.HIGH)
